# Fritzing sketch DHT22ReadoutAndVisualize (saved by Fritzing 0.9.2b)
circuit board: 8.46667cm x 5.64444cm
breadboards: 1

parts:
  DHT22 = Humidity and Temperature Sensor RHT03
  R1 = Resistor [tolerance=±5% resistance=1k package=THT]
  MVPROG1 = MicroView with Programmer [part_number=MicroView package="16pin wide"]

nets (from the schematic view):
  N1: DHT22.Vcc, R1.Pin_0
  N2: DHT22.Data-signal, R1.Pin_1, MVPROG1.D3, MVPROG1.5V
  N3: DHT22.GND_2, MVPROG1.GND

custom parts:
  MicroView with Programmer: MicroView - Chip-sized Arduino with OLED display.

// code stored in the sketch: DHT22_auslesen_u_anzeigen.ino
#include <MicroView.h>
#include <DHT.h>

#define DHTPIN 3
#define DHTTYPE DHT22

DHT dht(DHTPIN, DHTTYPE);

void setGauge(double val);
int buttonPin = A0;
int buttonState = 0;
MicroViewWidget *widget;
int widgetState = -1;    //0 for temp, 1 for hum
float savedValue = 0.0;

void setup() {
  Serial.begin(9600);
  Serial.println("DHT22 - TEST!");
  dht.begin();
  uView.begin();
  uView.clear(PAGE);
  //pinMode(buttonPin, INPUT_PULLUP);
  //digitalWrite(buttonPin, LOW);
}

void loop() {
  
  float h = dht.readHumidity();
  float t = dht.readTemperature();
  buttonState = analogRead(buttonPin);
  
  if(isnan(t) || isnan(h) )
  {
    Serial.println("DHT22 konnte nicht ausgelesen werden");
  }
  else
  {
    if(buttonState > 800)
    {
      if(widgetState != 0)
      {
        uView.clear(PAGE);
        delete widget;
        widget = new MicroViewGauge(35, 17, -20, 80, WIDGETSTYLE0 + WIDGETNOVALUE);
        widgetState = 1;
        savedValue = -1.0;
      }
      if(savedValue != t)
      {
        uView.setCursor(widget->getX() - 8, widget->getY() + 11);
        uView.print(" C ");
        setGauge(t);
        savedValue = t;
        returnValuesSerial("Temperatur", t, h);
      }
    }
    else
    {
      if(widgetState != 1)
      {
        uView.clear(PAGE);
        delete widget;
        widget = new MicroViewGauge(35, 17, 0, 100, WIDGETSTYLE0 + WIDGETNOVALUE);
        widgetState = 1;
        savedValue = -1.0;
      }
      if(savedValue != h)
      {
        uView.setCursor(widget->getX() - 8, widget->getY() + 11);
        uView.print(" \x25 ");
        setGauge(h);
        savedValue = h;
        returnValuesSerial("Luftfeuchte", t, h); 
      } 
    }
  }
  delay(2000);
}

int ValueToUse(double value)
{
  return int(value); 
}

void setGauge(double val)
{
  widget->setValue(ValueToUse(val));
  uView.setCursor(widget->getX() - 17, widget->getY() + 19);
  uView.setFontType(1);
  if(val < 100)
  {
    uView.print(' ');
  }
  uView.print((float)val);
  uView.setFontType(0);
  uView.display();
}

void returnValuesSerial(String Mode, float temp, float hum)
{
	Serial.print("Aktueller Modus: ");
	Serial.println(Mode);
  Serial.print("Luftfeuchte: ");
  Serial.print(hum);
  Serial.print("%\t");
  Serial.print("Temperatur: ");
  Serial.print(temp);
  Serial.println("C");
}

// code stored in the sketch: Readout_DHT22_and_visualize.ino
/* ==========================================================
 * Little programm for an MicroView. Basic is an Arduino UNO
 * but there is a display on it.
 * Read out temp and humidity from a DHT22 and show it
 * on two MicroViewWidgets. Also the information will be
 * shown at the serial monitor.
 * Code created by: M3taKn1ght
 * Created at:   2015/11/05 by M3taKn1ght
 * Last changes: 2015/11/14 by M3taKn1ght
 * ==========================================================
 */
//Include needed libs, see ReadMe
#include <MicroView.h>
#include <DHT.h>

//Define Pin and DHT-typ
#define DHTPIN 3
#define DHTTYPE DHT22

DHT dht(DHTPIN, DHTTYPE);

MicroViewWidget *widgetTemp;
MicroViewWidget *widgetHumi;

//Setup befor it starts
void setup() {
  Serial.begin(9600); //Init serial
  Serial.println("DHT22 - Temp and Humi!");
  dht.begin();    //init dht
  uView.begin();  //init uView
  uView.clear(PAGE);  //clear screen
  StartUp();
  /* ========================================
   * Gauge style 0 with numeric value
   * for widgetTemp a range between -20 to 80
   * for widgetHumi a range between 0 to 100
   * ========================================
   */
  widgetTemp = new MicroViewGauge(15, 24, -20, 80, WIDGETSTYLE0);
  widgetHumi = new MicroViewGauge(48, 24, 0, 100, WIDGETSTYLE0);
}

//Lets begin with the fun
void loop() {
  
  float h = dht.readHumidity();
  float t = dht.readTemperature();
  
  //Check if informations are valid
  if(isnan(t) || isnan(h) )
  {
    Serial.println("Cant't get informations from DHT22");
  }
  else
  {
    updateWidget(t, h);
    returnValuesSerial(t, h);
  }

  delay(2000);  //wait for two seconds
}

//Function to set informations for widget
void updateWidget(float temp, float humi)
{
  widgetTemp->setValue(roundValue(temp));
  widgetHumi->setValue(roundValue(humi));
  uView.display();
}

//Function to write header above the widgets
void StartUp(){
  uView.clear(PAGE);
  uView.setCursor(0, 0);
  uView.print(" Temp Humi");
  uView.display();
}

//Function to write basic information to serial monitor
void returnValuesSerial(float temp, float hum)
{
  Serial.print("Humidity: ");
  Serial.print(hum);
  Serial.print("%\t");
  Serial.print("Temperature: ");
  Serial.print(temp);
  Serial.println("C");
}

//Function to round given float value
int roundValue(float value){
  double rounded = 0.0;
  if(value <= 0){
    rounded = value - 0.5;
    return (int)rounded;
  }
  else{
    rounded = value + 0.5;
    return (int)rounded;
  }
}

// code stored in the sketch: Source.ino
/*
 Little programm for an MicroView. Basic is an Arduino UNO but there is a display on it.
With a DHT22 we read out temp and humidity. We will show this on the screen and write some
diags through the serial port.

Code created by: M3taK1ght
Version:			0.0.1
Created at: 	2015/11/05
Last changes:	2015/11/05 by M3taK1ght
 */

#include <MicroView.h>
#include <DHT.h>

//Define Pin and DHT-typ
#define DHTPIN 3
#define DHTTYPE DHT22

DHT dht(DHTPIN, DHTTYPE);

void setGauge(double val);	
int buttonPin = A0;				//Analog input for switch
int buttonState = 0;			//Stores the analog value
MicroViewWidget *widget;
int widgetState = -1;			// 0 for temp, 1 for hum
float savedValue = 0.0;		// Save last value from DHT22

//StartUp
void setup() {
  Serial.begin(9600);	//Init serial
  Serial.println("DHT22 - TEST!");
  dht.begin();		//init dht
  uView.begin();	//init uView
  uView.clear(PAGE);	//clear screen
}

//Lets begin with the fun
void loop() {
  
  float h = dht.readHumidity();
  float t = dht.readTemperature();
  buttonState = analogRead(buttonPin);	//I don't know why digitalRead is not working at this point
  
	//Check if informations are valid
  if(isnan(t) || isnan(h) )
  {
    Serial.println("Cant't get informations from DHT22");
  }
  else
  {
    if(buttonState > 800)		
    {
			//If object is not created for Temp
      if(widgetState != 0)
      {
        uView.clear(PAGE);
        delete widget;		//delete pointer
        widget = new MicroViewGauge(35, 17, -20, 80, WIDGETSTYLE0 + WIDGETNOVALUE);	//Create new widget 
        widgetState = 1;		//Save for which mode widget was created
        savedValue = -100.0;	//Needed for the first startup
      }
      if(savedValue != t)
      {
        uView.setCursor(widget->getX() - 8, widget->getY() + 11);
        uView.print(" C ");
        setGauge(t);
        savedValue = t;
        returnValuesSerial("Temperature", t, h);
      }
    }
    else
    {
      if(widgetState != 1)
      {
        uView.clear(PAGE);
        delete widget;
        widget = new MicroViewGauge(35, 17, 0, 100, WIDGETSTYLE0 + WIDGETNOVALUE);
        widgetState = 1;
        savedValue = -100.0;
      }
      if(savedValue != h)
      {
        uView.setCursor(widget->getX() - 8, widget->getY() + 11);
        uView.print(" \x25 ");	//Hex for "%"
        setGauge(h);
        savedValue = h;
        returnValuesSerial("Humidity", t, h); 
      } 
    }
  }
  delay(2000);	//wait for two seconds
}

//Function to get an int from double
int ValueToUse(double value)
{
  return int(value); 
}

//Function to set informations for widget
void setGauge(double val)
{
  widget->setValue(ValueToUse(val));
  uView.setCursor(widget->getX() - 17, widget->getY() + 19);
  uView.setFontType(1);
  
	uView.print((float)val);
  uView.setFontType(0);
  uView.display();
}

//Function to write basic information to serial monitor
void returnValuesSerial(String Mode, float temp, float hum)
{
	Serial.print("Current Mode: ");
	Serial.println(Mode);
  Serial.print("Humidity: ");
  Serial.print(hum);
  Serial.print("%\t");
  Serial.print("Temperature: ");
  Serial.print(temp);
  Serial.println("C");
}
